// Logisim project mips-add.circ as structural Verilog: 4 circuits, main circuit main
module main (
  output [31:0] out_1,
  output [5:0] out_2,
  output [31:0] PCCounter
);

  wire clock_1_out, registerfile_1_p1, registerfile_1_p7;
  wire [4:0] multiplexer_1_out;
  wire [6:0] rom_1_data;
  wire [31:0] adder_1_out, bit_extender_1_out, multiplexer_2_out, registerfile_1_p8;

  ROM #(.addrWidth(6), .dataWidth(7)) rom_1 (.addr(out_1[31:26]), .data(rom_1_data));
  Clock clock_1 (.out(clock_1_out));
  PC pc_1 (.NewBits(adder_1_out), .clk(clock_1_out), .CurrentBits(PCCounter));
  Adder #(.width(32)) adder_1 (.a(32'h4), .b(PCCounter), .out(adder_1_out));  // open: cin, cout
  // MIPSProgramROM mipsprogramrom_1: pin names not known; wires that end beside it: PCCounter
  assign bit_extender_1_out = {{16{out_1[15]}}, out_1[15:0]};  // Bit_Extender bit_extender_1
  Multiplexer #(.width(5), .enable("false")) multiplexer_1 (
    .in0(out_1[15:11]), .in1(out_1[20:16]), .out(multiplexer_1_out), .sel(rom_1_data[1]));
  // RegisterFile registerfile_1: pin names not known; wires that end beside it: registerfile_1_p1, clock_1_out, rom_1_data[0], multiplexer_1_out, out_1[25:21], out_1[20:16], registerfile_1_p7, registerfile_1_p8
  Multiplexer #(.width(32), .enable("false")) multiplexer_2 (
    .in0(registerfile_1_p8), .in1(bit_extender_1_out), .out(multiplexer_2_out), .sel(rom_1_data[2]));
  // Mips_ALU mips_alu_1: pin names not known; wires that end beside it: registerfile_1_p7, multiplexer_2_out, rom_1_data[6:3], registerfile_1_p1

  assign out_2 = out_1[31:26];

  // Notes on the sheet:
  //   contents of rom_1 (hex, n*v repeats v):
  //   11 7*0 17 17
  //   contents of mipsprogramrom_1 (hex, n*v repeats v):
  //   addiu $s1, $zero, 2 addu $s2, $s0, $s1
endmodule

module Remember1bit (
  input  NewBit,
  input  clk,
  output CurrentBit
);

  wire xor_1_out;

  xor xor_1 (xor_1_out, CurrentBit, NewBit);
  T_Flip_Flop t_ff_1 (.T(xor_1_out), .clk(clk), .Qn(CurrentBit));  // open: Q, reset, preset

  // Notes on the sheet:
  //   CurrentBit: pull=down
endmodule

module Remember4bit (
  input  [7:0] NewBits,
  input  clk,
  output [7:0] CurrentBit
);

  Remember1bit remember1bit_1 (.NewBit(NewBits[0]), .clk(clk), .CurrentBit(CurrentBit[0]));
  Remember1bit remember1bit_2 (.NewBit(NewBits[1]), .clk(clk), .CurrentBit(CurrentBit[1]));
  Remember1bit remember1bit_3 (.NewBit(NewBits[2]), .clk(clk), .CurrentBit(CurrentBit[2]));
  Remember1bit remember1bit_4 (.NewBit(NewBits[3]), .clk(clk), .CurrentBit(CurrentBit[3]));
  Remember1bit remember1bit_5 (.NewBit(NewBits[4]), .clk(clk), .CurrentBit(CurrentBit[4]));
  Remember1bit remember1bit_6 (.NewBit(NewBits[5]), .clk(clk), .CurrentBit(CurrentBit[5]));
  Remember1bit remember1bit_7 (.NewBit(NewBits[6]), .clk(clk), .CurrentBit(CurrentBit[6]));
  Remember1bit remember1bit_8 (.NewBit(NewBits[7]), .clk(clk), .CurrentBit(CurrentBit[7]));

  // Notes on the sheet:
  //   clk: pull=up
  //   NewBits: pull=down
endmodule

module PC (
  input  [31:0] NewBits,
  input  clk,
  output [31:0] CurrentBits
);

  Remember4bit remember4bit_1 (.NewBits(NewBits[7:0]), .clk(clk), .CurrentBit(CurrentBits[7:0]));
  Remember4bit remember4bit_2 (.NewBits(NewBits[15:8]), .clk(clk), .CurrentBit(CurrentBits[15:8]));
  Remember4bit remember4bit_3 (.NewBits(NewBits[23:16]), .clk(clk), .CurrentBit(CurrentBits[23:16]));
  Remember4bit remember4bit_4 (.NewBits(NewBits[31:24]), .clk(clk), .CurrentBit(CurrentBits[31:24]));
endmodule
